# Fritzing sketch Test-Bench-Schematic (saved by Fritzing 0.9.3b)
breadboards: 1

parts:
  hc-sr1 = hc-sr04
  Composant1 = Arduino Uno (Rev3) - ICSP
  DS1 = DS18B20 1-Wire Temperature Sensor [part_number=DS18B20]
  MOTOR1 = 28BYJ-48 Stepper Motor
  X1 = X113647 Stepper Driver Board [package=board]
  S1 = Round Pushbutton

nets:
  VCC: hc-sr1.VCC, Composant1.5V, DS1.VDD
  N1: hc-sr1.Trig, Composant1.D2
  N2: hc-sr1.Echo, Composant1.D3_PWM
  N3: hc-sr1.GND, Composant1.D4
  N4: Composant1.ICSP_MOSI, Composant1.D11_PWM/MOSI, X1.IN4
  N5: Composant1.D8, X1.IN1
  N6: Composant1.D9_PWM, X1.IN2
  N7: Composant1.D10_PWM/SS, X1.IN3
  N8: Composant1.D5_PWM, S1.leg1
  N9: Composant1.D7, DS1.DQ
  GND: Composant1.GND, DS1.GND, S1.leg0
  N10: MOTOR1.BLUE, X1.BLUE
  N11: MOTOR1.PINK, X1.PINK
  N12: MOTOR1.RED, X1.RED
  N13: MOTOR1.ORANGE, X1.ORANGE
  N14: MOTOR1.YELLOW, X1.YELLOW

custom parts:
  28BYJ-48 Stepper Motor: 28BYJ-48 gear-reduction stepper motor (small)
  X113647 Stepper Driver Board: A common stepper motor driver board based on ULN2003APG darlington array
